# Fritzing sketch fritzing sketch - cube project (saved by Fritzing 0.9.2b)
circuit board: 8.46667cm x 5.64444cm
breadboards: 1

parts:
  SPI_SSD1 = OLED 0.95" 96x64 SPI SSD1331
  Part1 = Photon
  LED1 = RGB LED (com. anode, rbg) [package="5 mm [THT]"]
  S1 = Momentary Switch [package=ksa_sealed_tac_switch]
  R1 = Resistor [tolerance=±5% resistance=220 package=THT]
  R2 = Resistor [tolerance=±5% resistance=220 package=THT]
  R4 = Resistor [tolerance=±5% resistance=220 package=THT]
  R5 = Resistor [tolerance=±5% resistance=220 package=THT]

nets:
  VCC: SPI_SSD1.VCC, Part1.VIN, R1.Pin_0
  GND: SPI_SSD1.GND, Part1.GND
  N1: SPI_SSD1.DIN, Part1.A5
  N2: SPI_SSD1.CLK, Part1.A3
  N3: SPI_SSD1.CS, Part1.D5
  N4: SPI_SSD1.D/C, Part1.D4
  N5: SPI_SSD1.RES, Part1.D3
  N6: Part1.WKP, R4.Pin_1
  N7: Part1.D0, S1.1, S1.2
  N8: Part1.D1, R2.Pin_0
  N9: Part1.D2, R5.Pin_1
  N10: LED1.red_cathode, R2.Pin_1
  N11: LED1.blue_cathode, R5.Pin_0
  N12: LED1.green_cathode, R4.Pin_0
  N13: S1.3, S1.4, R1.Pin_1
